# Fritzing sketch PhotoComputer (saved by Fritzing 0.9.3b)
circuit board: 8.46667cm x 5.64444cm
breadboards: 1

parts:
  Onderdeel1 = Arduino Uno (Rev3)
  LCM1602_IIC1 = LCM1602 IIC [part_number="LCM1602 IIC" chip_label="LCM1602 IIC" package="DIP (Dual Inline) [THT]"]
  LCD1 = LCD screen
  PCB2 = RTC_DS1302_module
  S5 = Pushbutton [package="[THT]"]
  S6 = Pushbutton [package="[THT]"]
  S3 = Pushbutton [package="[THT]"]
  S1 = Pushbutton [package="[THT]"]
  S4 = Pushbutton [package="[THT]"]
  S2 = Pushbutton [package="[THT]"]
  R5 = Resistor [tolerance=±5% resistance=68k package=THT]
  R6 = Resistor [tolerance=±5% resistance=82k package=THT]
  R2 = Resistor [tolerance=±5% resistance=10k package=THT]
  R4 = Resistor [tolerance=±5% resistance=4.7k package=THT]
  R3 = Resistor [tolerance=±5% resistance=22k package=THT]
  J4 = Piezo Speaker
  R8 = Resistor [tolerance=±5% resistance=100 package=THT]
  J5 = Nikon Connector [package=THT]
  R7 = Resistor [tolerance=±5% resistance=100k package=THT]
  R1 = Resistor [tolerance=±5% resistance=47k package=THT]
  U1 = TLP621 [package=THT]
  U2 = TLP621 [package=THT]
  D1 = Diode [package=diode-hv]
  R9 = Resistor [tolerance=±5% resistance=220 package=THT]
  R10 = Resistor [tolerance=±5% resistance=220 package=THT]

nets:
  N1: Onderdeel1.A0, S5.Pin_3, S5.Pin_4, S6.Pin_3, S6.Pin_4, S3.Pin_3, S3.Pin_4, S1.Pin_3, S1.Pin_4, S4.Pin_3, S4.Pin_4, S2.Pin_3, S2.Pin_4, R7.Pin_1
  N2: Onderdeel1.A4/SDA, LCM1602_IIC1.SDA
  N3: Onderdeel1.A5/SCL, LCM1602_IIC1.SCL
  N4: Onderdeel1.D8, J4.pin2
  N5: Onderdeel1.D9_PWM, R9.Pin_0
  N6: Onderdeel1.D10_PWM/SS, R10.Pin_1
  N7: Onderdeel1.D11_PWM/MOSI, PCB2.RST
  N8: Onderdeel1.D12/MISO, PCB2.DAT
  N9: Onderdeel1.D13/SCK, PCB2.CLK
  VCC: Onderdeel1.5V, LCM1602_IIC1.VCC, PCB2.VCC, R5.Pin_0, R6.Pin_1, R2.Pin_0, R4.Pin_0, R3.Pin_0, R1.Pin_0
  GND: Onderdeel1.GND, LCM1602_IIC1.GND, PCB2.GND, R8.Pin_0, R7.Pin_0, U1.Pin_4, U2.Pin_4
  VSS: LCM1602_IIC1.VSS, LCD1.VSS
  VDD: LCM1602_IIC1.VDD, LCD1.VDD
  N10: LCM1602_IIC1.V0, LCD1.V0
  N11: LCM1602_IIC1.RS, LCD1.RS
  N12: LCM1602_IIC1.RW, LCD1.R/W
  N13: LCM1602_IIC1.E, LCD1.E
  N14: LCM1602_IIC1.D0, LCD1.DB0
  N15: LCM1602_IIC1.D1, LCD1.DB1
  N16: LCM1602_IIC1.D2, LCD1.DB2
  N17: LCM1602_IIC1.D3, LCD1.DB3
  N18: LCM1602_IIC1.D4, LCD1.DB4
  N19: LCM1602_IIC1.D5, LCD1.DB5
  N20: LCM1602_IIC1.D6, LCD1.DB6
  N21: LCM1602_IIC1.D7, LCD1.DB7
  N22: LCM1602_IIC1.A, LCD1.LED+
  N23: LCM1602_IIC1.K, LCD1.LED-
  N24: LCM1602_IIC1.LED_A, LCM1602_IIC1.LED_B
  N25: S5.Pin_1, S5.Pin_2, R5.Pin_1
  N26: S6.Pin_1, S6.Pin_2, R6.Pin_0
  N27: S3.Pin_1, S3.Pin_2, R3.Pin_1
  N28: S1.Pin_1, S1.Pin_2, R1.Pin_1
  N29: S4.Pin_1, S4.Pin_2, R4.Pin_1
  N30: S2.Pin_1, S2.Pin_2, R2.Pin_1
  N31: J4.pin1, R8.Pin_1
  N32: J5.Focus, D1.C
  N33: J5.GND, U1.Pin_1, U2.Pin_1
  N34: J5.Shoot, U2.Pin_2
  N35: U1.Pin_2, D1.A
  N36: U1.Pin_3, R9.Pin_1
  N37: U2.Pin_3, R10.Pin_0

notes:
  CameraConnector
  Keyboard
  Up
  Down
  Left
  Right

custom parts:
  LCM1602 IIC: I2C-Module to use a 1602 or 2004 LCD on with the wire.h libory Serial LCD Modul
  RTC_DS1302_module: Arduino module DS1302 SPI Real Time Clock

// code stored in the sketch: AnalogReadSerial2LCD_LED.ino
#include <Wire.h>
#include <LiquidCrystal_I2C.h>

LiquidCrystal_I2C lcd(0x27, 16, 2);   // adress and format LCD

const int analogInPin = A0;           // Analog input pin that the potentiometer is attached to
const int analogOutPin = 9;           // Analog output pin that the LED is attached to

int sensorValue = 0;                  // value read from the pot
int outputValue = 0;                  // value output to the PWM (analog out)

void setup() {
  lcd.init();                         // init LCD
  lcd.backlight();
  lcd.home();
  lcd.setCursor(5, 0);                // place static text
  lcd.print("ADC = ");
  lcd.setCursor(15, 0);
  lcd.print("V");
  lcd.setCursor(0, 1);
  lcd.print("LED : ");
  lcd.setCursor(12, 1);
  lcd.print("%");
  Serial.begin(9600);                 // optional serial monitor
}

void loop() {
  int sensorValue = analogRead(analogInPin);          // read analog A0 en store in sensorValue
  float voltValue = 5.0 / 1024.0 * sensorValue;       // calculate volt at analog A0 and store in voltValue
  float percentValue = sensorValue / 1024.0 * 100.0;  // calculate percentage analog A0 and store in percentValue
  outputValue = map(sensorValue, 0, 1023, 0, 255);    // map analog input to analog output and store in outputValue
  analogWrite(analogOutPin, outputValue);             // write outputValue to analogOutPin

  lcd.setCursor(0, 0);                                // set cursor at deserid position
  leadingZeros(sensorValue, 4);                       // print sensorvalue with number of leading-characters (0 or space as specified in function leadingZeros)
  lcd.setCursor(10, 0);                               // set cursor at deserid position
  lcd.print(voltValue);                               // print voltValue
  lcd.setCursor(6, 1);                                // set cursor at deserid position
  lcd.print(percentValue);                            // print percentValue

  Serial.print("sensor = " );                         // print the results to the serial monitor:
  Serial.print(sensorValue);
  Serial.print("\t output = ");
  Serial.print(outputValue);
  Serial.print("\t procent = ");
  Serial.println(percentValue);

  delay(1000);                                        // set delay
}

void leadingZeros( int value, int width) {            // display result with leading characters
  char valueStr[6];                                   // large enough to hold an int
  itoa (value, valueStr, 10);                         // itoa converts int to string
  int len = strlen(valueStr);                         // calculate length of valueStr
  if (len < width) {
    len = width - len;
    while (len--)
      lcd.print(' ');                                 // for leading zeros place '0' between (), for leading spaces place ' ' between ()
  }
  lcd.print(valueStr);
}
